# Fritzing sketch dock_device_connection (saved by Fritzing 0.9.6b)

parts:
  J1 = STM32 Nucleo boards
  LED1 = LED - 5mm [color="Red (633nm)" package="5 mm [THT]"]
  R1 = Resistor [tolerance=±5% resistance=220 package=THT]
  S1 = SWITCH-MOMENTARY-2 [package=tactile-pth-12mm]

nets:
  N1: J1.GND#1157, R1.Pin_0
  N2: J1.D3_PWM, S1.2
  N3: J1.D4, LED1.anode
  N4: J1.GND#1189, S1.1
